// Logisim project home.circ as structural Verilog: 5 circuits, main circuit main
module main (
);

  wire button_1_out, clock_1_out, comb_1_g, comb_1_r, comb_1_rs, comb_1_y;
  wire [1:0] comb_1_nx, dff2_1_q;
  wire [2:0] timer3_1_q;

  Clock clock_1 (.out(clock_1_out));
  Button button_1 (.out(button_1_out));
  comb comb_1 (
    .Timer(timer3_1_q), .pr(dff2_1_q), .R(comb_1_r), .Y(comb_1_y), .G(comb_1_g), .nx(comb_1_nx),
    .rs(comb_1_rs));
  timer3 timer3_1 (.q(timer3_1_q), .clock(clock_1_out), .reset(comb_1_rs), .clear(button_1_out));
  dff2 dff2_1 (.D(comb_1_nx), .in_2(clock_1_out), .Q(dff2_1_q));  // open: rst
  LED led_1 (.in(comb_1_r));
  LED led_2 (.in(comb_1_y));
  LED led_3 (.in(comb_1_g));
endmodule

module dff2 (
  input  [1:0] D,
  input  in_2,
  input  rst,
  output [1:0] Q
);

  D_Flip_Flop d_ff_1 (.clk(in_2), .D(D[0]), .Q(Q[0]), .reset(rst));  // open: Qn, preset, en
  D_Flip_Flop d_ff_2 (.clk(in_2), .D(D[1]), .Q(Q[1]), .reset(rst));  // open: Qn, preset, en
endmodule

module comb (
  input  [2:0] Timer,
  input  [1:0] pr,
  output R,
  output Y,
  output G,
  output [1:0] nx,
  output rs
);

  wire _2_out, _4_out, _6_out, and_1_out, and_2_out, and_8_out, and_9_out, and_10_out, and_11_out, or_1_out,
       or_2_out;

  and _2 (_2_out, ~Timer[0], Timer[1], ~Timer[2]);  // AND_Gate
  and _4 (_4_out, ~Timer[0], ~Timer[1], Timer[2]);  // AND_Gate
  and _6 (_6_out, ~Timer[0], Timer[1], Timer[2]);  // AND_Gate
  and and_1 (and_1_out, _4_out, pr[0], pr[1]);
  or or_1 (or_1_out, pr[0], _6_out);
  and and_2 (and_2_out, pr[0], _2_out);
  and and_3 (nx[0], ~and_1_out, or_1_out);  // AND_Gate
  and and_4 (nx[1], ~and_1_out, or_2_out);  // AND_Gate
  or or_2 (or_2_out, and_2_out, pr[1]);
  and and_5 (R, pr[0], pr[1]);
  and and_6 (Y, pr[0], ~pr[1]);  // AND_Gate
  and and_7 (G, ~pr[0], ~pr[1]);  // AND_Gate
  and and_8 (and_8_out, pr[0], ~nx[0]);  // AND_Gate
  and and_9 (and_9_out, nx[0], ~pr[0]);  // AND_Gate
  and and_10 (and_10_out, pr[1], ~nx[1]);  // AND_Gate
  and and_11 (and_11_out, nx[1], ~pr[1]);  // AND_Gate
  or or_3 (rs, and_8_out, and_9_out, and_10_out, and_11_out);
endmodule

module dff3 (
  input  [2:0] D,
  input  in_2,
  input  rst,
  output [2:0] Q
);

  D_Flip_Flop d_ff_1 (.clk(in_2), .D(D[0]), .Q(Q[0]), .reset(rst));  // open: Qn, preset, en
  D_Flip_Flop d_ff_2 (.clk(in_2), .D(D[1]), .Q(Q[1]), .reset(rst));  // open: Qn, preset, en
  D_Flip_Flop d_ff_3 (.clk(in_2), .D(D[2]), .Q(Q[2]), .reset(rst));  // open: Qn, preset, en
endmodule

module timer3 (
  input  clock,
  input  clear,
  input  reset,
  output [2:0] q
);

  wire and_1_out, or_1_out;

  Counter #(.width(3), .max('h7), .trigger("falling")) counter_1 (
    .Q(q), .clk(clock), .clr(or_1_out));  // open: load, D, count, carry
  and and_1 (and_1_out, clock, reset);
  or or_1 (or_1_out, and_1_out, clear);
endmodule
